// Logisim project 1214SHIFT.circ as structural Verilog: 1 circuit, main circuit main
module main (
  input  [31:0] Input,
  input  [4:0] Shamt,
  input  [4:0] Rs_value,
  input  [5:0] Func,
  output [31:0] Output
);

  wire [4:0] adder_1_out;
  wire [31:0] shifter_1_out, shifter_2_out, shifter_3_out, shifter_4_out, shifter_5_out, shifter_6_out;

  Adder #(.width(5)) adder_1 (.a(Shamt), .b(Rs_value), .out(adder_1_out));  // open: cin, cout
  Shifter #(.width(32)) shifter_1 (.in(Input), .\dist (Shamt), .out(shifter_1_out));
  Shifter #(.width(32), .shift("lr")) shifter_2 (.in(Input), .\dist (Shamt), .out(shifter_2_out));
  Shifter #(.width(32), .shift("ar")) shifter_3 (.in(Input), .\dist (Shamt), .out(shifter_3_out));
  Shifter #(.width(32)) shifter_4 (.in(Input), .\dist (adder_1_out), .out(shifter_4_out));
  Shifter #(.width(32), .shift("lr")) shifter_5 (.in(Input), .\dist (adder_1_out), .out(shifter_5_out));
  Shifter #(.width(32), .shift("ar")) shifter_6 (.in(Input), .\dist (adder_1_out), .out(shifter_6_out));
  Multiplexer #(.select(3), .width(32)) multiplexer_1 (
    .in0(shifter_1_out), .in2(shifter_2_out), .in3(shifter_3_out), .in4(shifter_4_out), .in6(shifter_5_out),
    .in7(shifter_6_out), .out(Output), .sel(Func[2:0]));  // open: in1, in5, en
endmodule
