// Logisim project ALU_Control.circ as structural Verilog: 1 circuit, main circuit main
module main (
  input  ALUOp1,
  input  ALUOp0,
  input  Func5,
  input  Func4,
  input  Func3,
  input  Func2,
  input  Func1,
  input  Func0,
  output ALUControl2,
  output ALUControl1,
  output ALUControl0
);

  wire and_1_out, and_2_out, and_3_out, and_4_out, and_5_out, and_6_out, and_7_out, and_8_out, and_9_out,
       not_1_out, not_2_out, not_3_out, not_4_out, not_5_out, not_6_out, not_7_out, not_8_out, not_9_out,
       not_10_out;

  not not_1 (not_1_out, Func5);
  not not_2 (not_2_out, Func4);
  not not_3 (not_3_out, Func3);
  not not_4 (not_4_out, Func1);
  not not_5 (not_5_out, ALUOp0);
  not not_6 (not_6_out, Func5);
  not not_7 (not_7_out, Func4);
  not not_8 (not_8_out, Func3);
  and and_1 (and_1_out, ALUOp1, Func3);
  and and_2 (and_2_out, ALUOp1, Func4, Func0);
  and and_3 (and_3_out, ALUOp1, Func5, Func0);
  and and_4 (and_4_out, ALUOp1, ALUOp0, Func0);
  and and_5 (and_5_out, ALUOp1, not_1_out, not_2_out, not_3_out, not_4_out, Func0);
  and and_6 (and_6_out, ALUOp1, Func3, Func1);
  and and_7 (and_7_out, ALUOp1, Func4, Func1);
  and and_8 (and_8_out, ALUOp1, Func5, Func1);
  not not_9 (not_9_out, ALUOp1);
  or or_1 (ALUControl1, not_9_out, and_9_out, not_10_out);
  and and_9 (and_9_out, not_5_out, not_6_out, not_7_out, not_8_out);
  not not_10 (not_10_out, Func2);
  or or_2 (ALUControl0, and_1_out, and_2_out, and_3_out, and_4_out);
  or or_3 (ALUControl2, ALUOp0, and_5_out, and_6_out, and_7_out, and_8_out);
endmodule
