// Logisim project CS_20195124_14_temp.circ as structural Verilog: 1 circuit, main circuit main
module main (
);

  wire AluSrc, and_1_out, Branch, CLK_out, Jump, main_3_zero, MemtoReg, MemWrite, RegDst, RegWrite, Reset_out;
  wire [2:0] ALUControl;
  wire [4:0] multiplexer_3_out;
  wire [5:0] Func, Op;
  wire [7:0] adder_1_out, multiplexer_1_out, multiplexer_2_out, PC_q, shifter_1_out;
  wire [8:0] main_3_y;
  wire [19:0] rom_1_data, shifter_1_out_2;
  wire [22:0] main_3_y_2;
  wire [27:0] bit_extender_2_out;
  wire [31:0] adder_2_out, bit_extender_1_out, bit_extender_3_out, main_2_rd1, main_2_rd2, main_4_output,
       main_4_rd, multiplexer_4_out, multiplexer_5_out, shifter_2_out;

  Multiplexer #(.width(8)) multiplexer_1 (
    .in0(adder_1_out), .in1(adder_2_out[7:0]), .out(multiplexer_1_out), .sel(and_1_out));  // open: en
  mips_MainControl_main main_1 (
    .opcode(Op), .Func(Func), .RegWrite(RegWrite), .RegDst(RegDst), .AluSrc(AluSrc), .MemWrite(MemWrite),
    .MemtoReg(MemtoReg), .ALUControl(ALUControl), .Jump(Jump), .Branch(Branch));
  Register PC (.D(multiplexer_2_out), .Q(PC_q), .clk(CLK_out), .clr(Reset_out));  // open: en
  Multiplexer #(.width(8)) multiplexer_2 (
    .in0(multiplexer_1_out), .in1(shifter_1_out), .out(multiplexer_2_out), .sel(Jump));  // open: en
  Clock CLK (.out(CLK_out));
  Button Reset (.out(Reset_out));
  Adder adder_1 (.a(PC_q), .b(8'h4), .out(adder_1_out));  // open: cin, cout
  assign bit_extender_1_out = {{24{1'b0}}, adder_1_out};  // Bit_Extender bit_extender_1
  ROM #(.addrWidth(6), .dataWidth(32)) rom_1 (.addr(PC_q[7:2]), .data({Op, rom_1_data, Func}));  // open: sel
  assign bit_extender_2_out = {{2{1'b0}}, {rom_1_data, Func}};  // Bit_Extender bit_extender_2
  // Probe on Op
  Multiplexer #(.width(5)) multiplexer_3 (
    .in0(rom_1_data[14:10]), .in1(rom_1_data[9:5]), .out(multiplexer_3_out), .sel(RegDst));  // open: en
  assign bit_extender_3_out = {{16{rom_1_data[9]}}, {rom_1_data[9:0], Func}};  // Bit_Extender bit_extender_3
  Shifter #(.width(28)) shifter_1 (.in(bit_extender_2_out), .\dist (5'b00010), .out({shifter_1_out_2, shifter_1_out}));
  regfile_main main_2 (
    .A1(rom_1_data[19:15]), .A2(rom_1_data[14:10]), .WE(RegWrite), .A3(multiplexer_3_out),
    .WD3(multiplexer_5_out), .CLK(CLK_out), .RD1(main_2_rd1), .RD2(main_2_rd2));
  Multiplexer #(.width(32)) multiplexer_4 (
    .in0(main_2_rd2), .in1(bit_extender_3_out), .out(multiplexer_4_out), .sel(AluSrc));  // open: en
  Shifter #(.width(32)) shifter_2 (.in(bit_extender_3_out), .\dist (5'b00010), .out(shifter_2_out));
  alu32_main main_3 (
    .F(ALUControl), .A(main_2_rd1), .B(multiplexer_4_out), .Y({main_3_y_2, main_3_y}), .Zero(main_3_zero));
  Adder #(.width(32)) adder_2 (.a(shifter_2_out), .b(bit_extender_1_out), .out(adder_2_out));  // open: cin, cout
  and and_1 (and_1_out, Branch, main_3_zero);
  dataMemory_main main_4 (
    .A(main_3_y), .CLK(CLK_out), .MemWrite(MemWrite), .WD(main_2_rd2), .RD(main_4_rd), .Output(main_4_output));
  Multiplexer #(.width(32)) multiplexer_5 (
    .in0({main_3_y_2, main_3_y}), .in1(main_4_rd), .out(multiplexer_5_out), .sel(MemtoReg));  // open: en
  _7_Segment_Display u_7_segment_display_1 (
    .g(main_4_output[6]), .f(main_4_output[7]), .a(main_4_output[0]), .b(main_4_output[1]),
    .e(main_4_output[5]), .d(main_4_output[4]), .c(main_4_output[3]), .dp(main_4_output[2]));
  _7_Segment_Display u_7_segment_display_2 (
    .g(main_4_output[14]), .f(main_4_output[15]), .a(main_4_output[8]), .b(main_4_output[9]),
    .e(main_4_output[13]), .d(main_4_output[12]), .c(main_4_output[11]), .dp(main_4_output[10]));
  _7_Segment_Display u_7_segment_display_3 (
    .g(main_4_output[22]), .f(main_4_output[23]), .a(main_4_output[16]), .b(main_4_output[17]),
    .e(main_4_output[21]), .d(main_4_output[20]), .c(main_4_output[19]), .dp(main_4_output[18]));
  _7_Segment_Display u_7_segment_display_4 (
    .g(main_4_output[30]), .f(main_4_output[31]), .a(main_4_output[24]), .b(main_4_output[25]),
    .e(main_4_output[29]), .d(main_4_output[28]), .c(main_4_output[27]), .dp(main_4_output[26]));
  Button \u_화면_확장용  ();  // open: out

  // Notes on the sheet:
  //   lw $t2, 32($0)
  //   0x8c0a0020
  //   add $t1, $t2, $t3
  //   0x014b4820
  //   sw $t1, 4($t2)
  //   0xad490004
  //   beq $t1, $t2, 4
  //   0x112a0004
  //   contents of rom_1 (hex, n*v repeats v):
  //   20010abb ac010000 2001730a ac010000 20015b73 ac010000 2001ca5b ac010000 2001d9ca ac010000 2001f9d9
  //   ac010000 20010bf9 ac010000 2001fb0b ac010000 2001dbfb ac010000 2001bbdb ac010000 8000000
  //   8비트의 주소만 사용하고 있기 때문에 28 + 4(PC의 상위 4비트)를 하지 않고 28비트 중에서 하위 8비트만 연결을 한다
  //   28 bit
  //   32 bit
  //   한림대학교 소프트웨어 융합 대학
  //   학번 : 20195124, 성명 : 김민석
  //   addi $1, $0, 0xFF
  //   sw $1, 0($0)
  //   200100ff
  //   ac010000
  //   Memory Mapped IO
endmodule
