// Logisim project dataMemory.circ as structural Verilog: 1 circuit, main circuit main
module main (
  input  [8:0] A,
  input  [31:0] WD,
  input  MemWrite,
  input  CLK,
  output [31:0] RD,
  output [31:0] Output
);

  wire and_1_out, nor_1_out, not_1_out;

  nor nor_1 (nor_1_out, A[8], A[7], A[6], A[5], A[4], A[3], A[2], A[1], A[0]);
  not not_1 (not_1_out, MemWrite);
  RAM #(.addrWidth(7), .dataWidth(32)) ram_1 (.addr(A[8:2]), .data(RD), .clk(CLK), .ld(not_1_out));  // open: sel, clr
  assign RD = MemWrite ? WD : 32'bz;  // Controlled_Buffer controlled_buffer_1
  and and_1 (and_1_out, nor_1_out, MemWrite);
  Register #(.width(32)) register_1 (.D(WD), .en(and_1_out), .Q(Output), .clk(CLK));  // open: clr

  // Notes on the sheet:
  //   ld : 1 --> memory value --> RD 
  //   Enable이 특정 상황(주소가 0이고(0번지) MemWrite가 1일 때)에만 값을 저장할 수 있도록 한다
endmodule
