// Logisim project mips_MainControl.circ as structural Verilog: 1 circuit, main circuit main
module main (
  input  [5:0] opcode,
  input  [5:0] Func,
  output RegWrite,
  output RegDst,
  output AluSrc,
  output Branch,
  output MemWrite,
  output MemtoReg,
  output Jump,
  output [2:0] ALUControl
);

  wire main_1_aluop0, main_1_aluop1;

  mips_MainDecoder_main main_1 (
    .op5(opcode[5]), .op4(opcode[4]), .op3(opcode[3]), .op2(opcode[2]), .op1(opcode[1]), .op0(opcode[0]),
    .RegWrite(RegWrite), .RegDst(RegDst), .AluSrc(AluSrc), .Branch(Branch), .MemWrite(MemWrite),
    .MemtoReg(MemtoReg), .ALUOp1(main_1_aluop1), .ALUOp0(main_1_aluop0), .Jump(Jump));
  ALU_Control_main main_2 (
    .ALUOp1(main_1_aluop1), .ALUOp0(main_1_aluop0), .Func5(Func[5]), .Func4(Func[4]),
    .ALUControl2(ALUControl[2]), .Func3(Func[3]), .Func2(Func[2]), .Func1(Func[1]), .Func0(Func[0]),
    .ALUControl1(ALUControl[1]), .ALUControl0(ALUControl[0]));
endmodule
