// Logisim project mips_MainDecoder.circ as structural Verilog: 1 circuit, main circuit main
module main (
  input  op5,
  input  op4,
  input  op3,
  input  op2,
  input  op1,
  input  op0,
  output RegWrite,
  output RegDst,
  output AluSrc,
  output Branch,
  output MemWrite,
  output MemtoReg,
  output ALUOp1,
  output ALUOp0,
  output Jump
);

  wire and_2_out, and_3_out, not_1_out, not_2_out, not_3_out, not_4_out, not_5_out, not_6_out, not_7_out,
       not_8_out, not_9_out;

  not not_1 (not_1_out, op2);
  not not_2 (not_2_out, op1);
  not not_3 (not_3_out, op3);
  not not_4 (not_4_out, op3);
  not not_5 (not_5_out, op1);
  or or_1 (AluSrc, op1, op3);
  and and_1 (MemWrite, op5, op3);
  not not_6 (not_6_out, op3);
  not not_7 (not_7_out, op2);
  not not_8 (not_8_out, op1);
  not not_9 (not_9_out, op0);
  and and_2 (and_2_out, not_1_out, not_2_out);
  and and_3 (and_3_out, op5, not_3_out);
  and and_4 (RegDst, not_4_out, not_5_out);
  and and_5 (ALUOp1, not_6_out, not_7_out, not_8_out);
  and and_6 (Jump, op1, not_9_out);
  or or_2 (RegWrite, and_2_out, and_3_out);

  assign ALUOp0 = op2;
  assign Branch = op2;
  assign MemtoReg = op1;
endmodule
