// Logisim project mips_Shift.circ as structural Verilog: 1 circuit, main circuit main
module main (
  input  [31:0] Input,
  input  [4:0] Shamt,
  input  [4:0] Rs_value,
  input  [5:0] Func,
  output [31:0] Output
);

  wire [4:0] multiplexer_1_out;
  wire [31:0] shifter_1_out, shifter_2_out, shifter_3_out;

  Multiplexer #(.width(5)) multiplexer_1 (
    .in0(Shamt), .in1(Rs_value), .out(multiplexer_1_out), .sel(Func[2]));  // open: en
  Shifter #(.width(32)) shifter_1 (.in(Input), .\dist (multiplexer_1_out), .out(shifter_1_out));
  Shifter #(.width(32), .shift("lr")) shifter_2 (.in(Input), .\dist (multiplexer_1_out), .out(shifter_2_out));
  Shifter #(.width(32), .shift("ar")) shifter_3 (.in(Input), .\dist (multiplexer_1_out), .out(shifter_3_out));
  Multiplexer #(.select(2), .width(32)) multiplexer_2 (
    .in0(shifter_1_out), .in2(shifter_2_out), .in3(shifter_3_out), .out(Output), .sel(Func[1:0]));  // open: in1, en

  // Notes on the sheet:
  //   000 010 011
  //   100 110 111
endmodule
