// Logisim project mips_datapath.circ as structural Verilog: 1 circuit, main circuit main
module main (
  input  MemtoReg,
  input  MemWrite,
  input  Branch,
  input  [2:0] ALU_Ctrl,
  input  ALUSrc,
  input  WE,
  input  RegDst
);

  wire and_1_out, CLK_out, main_2_zero, Reset_out;
  wire [4:0] multiplexer_2_out;
  wire [7:0] adder_1_out, multiplexer_1_out, PC_q;
  wire [31:0] adder_2_out, bit_extender_1_out, bit_extender_2_out, main_1_rd1, main_1_rd2, main_2_y,
       main_3_rd, multiplexer_3_out, multiplexer_4_out, rom_1_data, shifter_1_out;

  Register PC (.D(multiplexer_1_out), .Q(PC_q), .clk(CLK_out), .clr(Reset_out));  // open: en
  Multiplexer #(.width(8)) multiplexer_1 (
    .in0(adder_1_out), .in1(adder_2_out[7:0]), .out(multiplexer_1_out), .sel(and_1_out));  // open: en
  Clock CLK (.out(CLK_out));
  Button Reset (.out(Reset_out));
  Adder adder_1 (.a(PC_q), .b(8'h4), .out(adder_1_out));  // open: cin, cout
  assign bit_extender_1_out = {{24{1'b0}}, adder_1_out};  // Bit_Extender bit_extender_1
  ROM #(.addrWidth(6), .dataWidth(32)) rom_1 (.addr(PC_q[7:2]), .data(rom_1_data));  // open: sel
  // Probe on rom_1_data[31:26]
  Multiplexer #(.width(5)) multiplexer_2 (
    .in0(rom_1_data[20:16]), .in1(rom_1_data[15:11]), .out(multiplexer_2_out), .sel(RegDst));  // open: en
  assign bit_extender_2_out = {{16{rom_1_data[15]}}, rom_1_data[15:0]};  // Bit_Extender bit_extender_2
  regfile_main main_1 (
    .A1(rom_1_data[25:21]), .A2(rom_1_data[20:16]), .WE(WE), .A3(multiplexer_2_out), .WD3(multiplexer_4_out),
    .CLK(CLK_out), .RD1(main_1_rd1), .RD2(main_1_rd2));
  Multiplexer #(.width(32)) multiplexer_3 (
    .in0(main_1_rd2), .in1(bit_extender_2_out), .out(multiplexer_3_out), .sel(ALUSrc));  // open: en
  Shifter #(.width(32)) shifter_1 (.in(bit_extender_2_out), .\dist (5'b00010), .out(shifter_1_out));
  alu32_main main_2 (.F(ALU_Ctrl), .A(main_1_rd1), .B(multiplexer_3_out), .Y(main_2_y), .Zero(main_2_zero));
  Adder #(.width(32)) adder_2 (.a(shifter_1_out), .b(bit_extender_1_out), .out(adder_2_out));  // open: cin, cout
  and and_1 (and_1_out, Branch, main_2_zero);
  dataMemory_main main_3 (
    .A(main_2_y[8:0]), .CLK(CLK_out), .MemWrite(MemWrite), .WD(main_1_rd2), .RD(main_3_rd));  // open: Output
  Multiplexer #(.width(32)) multiplexer_4 (
    .in0(main_2_y), .in1(main_3_rd), .out(multiplexer_4_out), .sel(MemtoReg));  // open: en

  // Notes on the sheet:
  //   한림대학교 소프트웨어 융합 대학
  //   학번 : 20195124, 성명 : 김민석
  //   lw $t2, 32($0)
  //   0x8c0a0020
  //   add $t1, $t2, $t3
  //   0x014b4820
  //   sw $t1, 4($t2)
  //   0xad490004
  //   beq $t1, $t2, 4
  //   0x112a0004
  //   contents of rom_1 (hex, n*v repeats v):
  //   8c0a0020 14b4820 ad490004 112a0004
endmodule
