// Logisim project p_09.circ as structural Verilog: 1 circuit, main circuit main
module main (
  output [31:0] out_1
);

  wire button_1_out, clock_1_out;
  wire [7:0] adder_1_out, register_1_q;

  Clock clock_1 (.out(clock_1_out));
  Button button_1 (.out(button_1_out));
  // Probe on register_1_q
  Register register_1 (.D(adder_1_out), .Q(register_1_q), .clk(clock_1_out), .clr(button_1_out));  // open: en
  // Probe on register_1_q[7:2]
  Adder adder_1 (.a(register_1_q), .b(8'h4), .out(adder_1_out));  // open: cin, cout
  ROM #(.addrWidth(6), .dataWidth(32)) rom_1 (.addr(register_1_q[7:2]), .data(out_1));  // open: sel

  // Notes on the sheet:
  //   PC
  //   Button
  //   Program Counter Simulation
  //   한림대 소프트웨어융합 대학 20195124 김민석
  //   Instruction Memory ROM
  //   contents of rom_1 (hex, n*v repeats v):
  //   20195124 22222222 33333333 44444444 55555555 66666666 77777777 88888888 99999999 aaaaaaaa bbbbbbbb
endmodule
