// Logisim project uaaaa.circ as structural Verilog: 1 circuit, main circuit main
module main (
  input  isShift
);

  wire AluSrc, and_1_out, Branch, CLK_out, Jump, main_4_zero, MemtoReg, MemWrite, RegDst, RegWrite, Reset_out;
  wire [2:0] ALUControl;
  wire [4:0] multiplexer_3_out;
  wire [5:0] Func, Op;
  wire [7:0] adder_1_out, multiplexer_1_out, multiplexer_2_out, PC_q, shifter_1_out;
  wire [19:0] rom_1_data, shifter_1_out_2;
  wire [27:0] bit_extender_2_out;
  wire [31:0] adder_2_out, bit_extender_1_out, bit_extender_3_out, main_2_output, main_3_rd1, main_3_rd2,
       main_4_y, main_5_output, main_5_rd, multiplexer_4_out, multiplexer_5_out, multiplexer_6_out,
       shifter_2_out;

  Multiplexer #(.width(8)) multiplexer_1 (
    .in0(adder_1_out), .in1(adder_2_out[7:0]), .out(multiplexer_1_out), .sel(and_1_out));  // open: en
  Multiplexer #(.width(8)) multiplexer_2 (
    .in0(multiplexer_1_out), .in1(shifter_1_out), .out(multiplexer_2_out), .sel(Jump));  // open: en
  Register PC (.D(multiplexer_2_out), .Q(PC_q), .clk(CLK_out), .clr(Reset_out));  // open: en
  Button Reset (.out(Reset_out));
  Clock CLK (.out(CLK_out));
  mips_MainControl_main main_1 (
    .opcode(Op), .Func(Func), .RegWrite(RegWrite), .RegDst(RegDst), .AluSrc(AluSrc), .MemWrite(MemWrite),
    .MemtoReg(MemtoReg), .ALUControl(ALUControl), .Jump(Jump), .Branch(Branch));
  Adder adder_1 (.a(PC_q), .b(8'h4), .out(adder_1_out));  // open: cin, cout
  assign bit_extender_1_out = {{24{1'b0}}, adder_1_out};  // Bit_Extender bit_extender_1
  ROM #(.addrWidth(6), .dataWidth(32)) rom_1 (.addr(PC_q[7:2]), .data({Op, rom_1_data, Func}));  // open: sel
  assign bit_extender_2_out = {{2{1'b0}}, {rom_1_data, Func}};  // Bit_Extender bit_extender_2
  // Probe on Op
  Multiplexer #(.width(5)) multiplexer_3 (
    .in0(rom_1_data[14:10]), .in1(rom_1_data[9:5]), .out(multiplexer_3_out), .sel(RegDst));  // open: en
  // Probe on Func
  // Probe on rom_1_data[4:0]
  Shifter #(.width(28)) shifter_1 (.in(bit_extender_2_out), .\dist (5'b00010), .out({shifter_1_out_2, shifter_1_out}));
  // Probe on multiplexer_3_out
  mips_Shift_main main_2 (
    .Input(multiplexer_6_out), .Shamt(rom_1_data[4:0]), .Func(Func), .Output(main_2_output));  // open: Rs_value
  assign bit_extender_3_out = {{16{rom_1_data[9]}}, {rom_1_data[9:0], Func}};  // Bit_Extender bit_extender_3
  // Probe on rom_1_data[14:10]
  // Probe on rom_1_data[19:15]
  Multiplexer #(.width(32)) multiplexer_4 (
    .in0(multiplexer_6_out), .in1(main_2_output), .out(multiplexer_4_out), .sel(isShift));  // open: en
  // Probe on multiplexer_4_out
  regfile_main main_3 (
    .A1(rom_1_data[19:15]), .A2(rom_1_data[14:10]), .WE(RegWrite), .A3(multiplexer_3_out),
    .WD3(multiplexer_4_out), .CLK(CLK_out), .RD1(main_3_rd1), .RD2(main_3_rd2));
  // Probe on ALUControl
  alu32_main main_4 (.F(ALUControl), .A(main_3_rd1), .B(multiplexer_5_out), .Y(main_4_y), .Zero(main_4_zero));
  Multiplexer #(.width(32)) multiplexer_5 (
    .in0(main_3_rd2), .in1(bit_extender_3_out), .out(multiplexer_5_out), .sel(AluSrc));  // open: en
  Shifter #(.width(32)) shifter_2 (.in(bit_extender_3_out), .\dist (5'b00010), .out(shifter_2_out));
  Adder #(.width(32)) adder_2 (.a(shifter_2_out), .b(bit_extender_1_out), .out(adder_2_out));  // open: cin, cout
  and and_1 (and_1_out, Branch, main_4_zero);
  dataMemory_main main_5 (
    .A(main_4_y[8:0]), .CLK(CLK_out), .MemWrite(MemWrite), .WD(main_3_rd2), .RD(main_5_rd),
    .Output(main_5_output));
  Multiplexer #(.width(32)) multiplexer_6 (
    .in0(main_4_y), .in1(main_5_rd), .out(multiplexer_6_out), .sel(MemtoReg));  // open: en
  _7_Segment_Display u_7_segment_display_1 (
    .g(main_5_output[6]), .f(main_5_output[7]), .a(main_5_output[0]), .b(main_5_output[1]),
    .e(main_5_output[5]), .d(main_5_output[4]), .c(main_5_output[3]), .dp(main_5_output[2]));
  _7_Segment_Display u_7_segment_display_2 (
    .g(main_5_output[14]), .f(main_5_output[15]), .a(main_5_output[8]), .b(main_5_output[9]),
    .e(main_5_output[13]), .d(main_5_output[12]), .c(main_5_output[11]), .dp(main_5_output[10]));
  _7_Segment_Display u_7_segment_display_3 (
    .g(main_5_output[22]), .f(main_5_output[23]), .a(main_5_output[16]), .b(main_5_output[17]),
    .e(main_5_output[21]), .d(main_5_output[20]), .c(main_5_output[19]), .dp(main_5_output[18]));
  _7_Segment_Display u_7_segment_display_4 (
    .g(main_5_output[30]), .f(main_5_output[31]), .a(main_5_output[24]), .b(main_5_output[25]),
    .e(main_5_output[29]), .d(main_5_output[28]), .c(main_5_output[27]), .dp(main_5_output[26]));
  Button \u_화면_확장용  ();  // open: out

  // Notes on the sheet:
  //   한림대학교 소프트웨어 융합 대학
  //   학번 : 20195124, 성명 : 김민석
  //   contents of rom_1 (hex, n*v repeats v):
  //   200100fc 11080 11882 12083
  //   28 bit
  //   32 bit
  //   Memory Mapped IO
endmodule
